// Logisim project fulladder.circ as structural Verilog: 1 circuit, main circuit main
module main (
  input  A,
  input  B,
  input  Cin,
  output SUM,
  output CARRY
);

  wire and_1_out, and_2_out, and_3_out;

  ExactlyOne xor_1 (.out(SUM), .in0(A), .in1(B), .in2(Cin));
  and and_1 (and_1_out, A, B);
  and and_2 (and_2_out, A, Cin);
  and and_3 (and_3_out, B, Cin);
  or or_1 (CARRY, and_1_out, and_2_out, and_3_out);

  // Notes on the sheet:
  //   FULL ADDER
endmodule
