// Logisim project nandgate.circ as structural Verilog: 1 circuit, main circuit main
module main (
  input  A,
  input  B,
  output Y
);

  wire and_1_out;

  and and_1 (and_1_out, A, B);
  not not_1 (Y, and_1_out);
endmodule
